# Fritzing sketch analogdcmotor (saved by Fritzing 0.9.3b)

parts:
  M1 = DC Motor
  S1 = H-Bridge with L298N
  M2 = DC Motor
  Parça1 = Arduino Uno (Rev3) - ICSP
  12V_DC = Power Jack [package=power_jack_smd]
  BT1 = Bluetooth HC-06u [package=THT]

nets:
  N1: M1.pin_1, S1.M2-02
  N2: M1.pin_2, S1.M2-01
  N3: S1.12V, 12V_DC.GNDBREAK
  GND: S1.GND, Parça1.GND, 12V_DC.GND, BT1.GND
  5V: S1.5V, Parça1.VIN
  N4: S1.ENA, Parça1.D6_PWM
  N5: S1.IN1, Parça1.D11_PWM/MOSI
  N6: S1.IN2, Parça1.D10_PWM/SS
  N7: S1.IN3, Parça1.D9_PWM
  N8: S1.IN4, Parça1.D8
  N9: S1.ENB, Parça1.D5_PWM
  N10: S1.M1-01, M2.pin_2
  N11: S1.M1-02, M2.pin_1
  N12: Parça1.D12/MISO, BT1.RXD
  N13: Parça1.D13/SCK, BT1.TXD
  3V3: Parça1.3V3, BT1.VCC

custom parts:
  H-Bridge with L298N: h-bridge
  Bluetooth HC-06u: Bluetooth HC-06 - face up, pins down 16.5mm x 37.5mm PCB
