# Fritzing sketch dijitaldcmotor (saved by Fritzing 0.9.3b)

parts:
  M1 = DC Motor
  S1 = H-Bridge with L298N
  M2 = DC Motor
  Parça1 = Arduino Uno (Rev3) - ICSP
  9V_DC = Power Jack [package=power_jack_smd]

nets:
  N1: M1.pin_1, S1.M2-02
  N2: M1.pin_2, S1.M2-01
  N3: S1.12V, 9V_DC.GNDBREAK
  N4: S1.ENA, Parça1.D6_PWM
  N5: S1.IN1, Parça1.D11_PWM/MOSI
  N6: S1.IN2, Parça1.D10_PWM/SS
  N7: S1.IN3, Parça1.D9_PWM
  N8: S1.IN4, Parça1.D8
  N9: S1.ENB, Parça1.D5_PWM
  N10: S1.M1-01, M2.pin_2
  N11: S1.M1-02, M2.pin_1

custom parts:
  H-Bridge with L298N: h-bridge
