# Fritzing sketch android_bluetooth_led_kontrol (saved by Fritzing 0.9.0b)

parts:
  Eleman1 = Arduino Uno (Rev3)
  Eleman2 = Bluetooth HC-05 Macho
  LED1 = LED - 5mm [color="Red (633nm)" package="5 mm [THT]"]

nets:
  N1: Eleman1.D13/SCK, LED1.anode
  GND: Eleman1.GND, Eleman2.GND, LED1.cathode
  N2: Eleman1.D0/RX, Eleman2.TXD
  N3: Eleman1.D1/TX, Eleman2.RXD
  3V3: Eleman1.3V3, Eleman2.VCC
