# Fritzing sketch bluetooth2string (saved by Fritzing 0.9.3b)
breadboards: 1

parts:
  Parça1 = Arduino Uno (Rev3)
  R1 = Resistor [tolerance=±5% resistance=1k package="1206 [SMD]"]
  R4 = Resistor [tolerance=±5% resistance=1k package="1206 [SMD]"]
  R5 = Resistor [tolerance=±5% resistance=1k package="1206 [SMD]"]
  BT1 = Bluetooth HC-06u [package=THT]

nets:
  N1: Parça1.D6_PWM, R1.Pin_0
  N2: Parça1.D7, BT1.TXD
  5V: Parça1.5V, BT1.VCC
  GND: Parça1.GND, R5.Pin_1, BT1.GND
  N3: R1.Pin_1, R4.Pin_0, BT1.RXD
  N4: R4.Pin_1, R5.Pin_0

custom parts:
  Bluetooth HC-06u: Bluetooth HC-06 - face up, pins down 16.5mm x 37.5mm PCB
