# Fritzing sketch hc-06 bluetooth (saved by Fritzing 0.9.3b)
breadboards: 1

parts:
  Parça1 = Arduino Uno (Rev3)
  BT1 = Bluetooth HC-06u [package=THT]
  R1 = Resistor [tolerance=±5% resistance=220 package="0603 [SMD]"]
  R4 = Resistor [tolerance=±5% resistance=220 package="0603 [SMD]"]
  R5 = Resistor [tolerance=±5% resistance=220 package="0603 [SMD]"]
  LED1 = LED - 5mm [color="Red (633nm)" package="5 mm [THT]"]
  LED2 = LED - 5mm [color="Red (633nm)" package="5 mm [THT]"]
  LED3 = LED - 5mm [color="Red (633nm)" package="5 mm [THT]"]

nets:
  N1: Parça1.D12/MISO, LED2.anode
  N2: Parça1.D13/SCK, LED1.anode
  GND: Parça1.GND, BT1.GND, R1.Pin_1, R4.Pin_1, R5.Pin_1
  N3: Parça1.D0/RX, BT1.TXD
  N4: Parça1.D1/TX, BT1.RXD
  N5: R1.Pin_0, LED1.cathode
  N6: R4.Pin_0, LED2.cathode
  N7: R5.Pin_0, LED3.cathode

custom parts:
  Bluetooth HC-06u: Bluetooth HC-06 - face up, pins down 16.5mm x 37.5mm PCB
