# Fritzing sketch rename (saved by Fritzing 0.9.3b)

parts:
  BT1 = Bluetooth HC-06u [package=THT]
  Parça1 = Arduino Uno (Rev3) - ICSP

nets:
  VCC: BT1.VCC, Parça1.3V3
  N1: BT1.TXD, Parça1.D0/RX
  N2: BT1.RXD, Parça1.D1/TX

custom parts:
  Bluetooth HC-06u: Bluetooth HC-06 - face up, pins down 16.5mm x 37.5mm PCB
